# Fritzing sketch comp (saved by Fritzing 0.9.3b)
breadboards: 1

parts:
  MTRX3 = LED Matrix - Serial Interface - Red/Green/Blue
  MTRX2 = LED Matrix - Serial Interface - Red/Green/Blue
  MTRX1 = LED Matrix - Serial Interface - Red/Green/Blue
  ChipKit_Uno32 = chipKIT Uno32 [package="SIP (Single Inline) [THT]"]
  ZS-042_RTC = ZS-042 RTC Module
  ESP-01 = ESP8266 ESP01 [part_number=ESP-01 package=THT]
  R1 = Resistor [tolerance=±5% resistance=10k package=THT]
  R2 = Resistor [tolerance=±5% resistance=10k package=THT]
  MTRX4 = LED Matrix - Serial Interface - Red/Green/Blue

nets:
  VCC: MTRX3.VCC, MTRX2.VCC, MTRX1.VCC, ChipKit_Uno32.5V, ZS-042_RTC.VCC, R1.Pin_1, R2.Pin_1, MTRX4.VCC
  N1: MTRX3.SCK, MTRX2.SCK, MTRX1.SCK, ChipKit_Uno32.D13, MTRX4.SCK
  N2: MTRX3.CS, MTRX2.CS, MTRX1.CS, ChipKit_Uno32.D10, MTRX4.CS
  N3: MTRX3.MISO, MTRX4.MOSI
  GND: MTRX3.GND, MTRX2.GND, MTRX1.GND, ChipKit_Uno32.GND, ZS-042_RTC.GND, ESP-01.GND, MTRX4.GND
  N4: MTRX3.MOSI, MTRX2.MISO
  N5: MTRX2.MOSI, MTRX1.MISO
  N6: MTRX1.MOSI, ChipKit_Uno32.D11
  N7: ChipKit_Uno32.D0RX, ESP-01.TXD
  N8: ChipKit_Uno32.D1TX, ESP-01.RXD
  N9: ChipKit_Uno32.D2, ESP-01.CH_PD
  N10: ChipKit_Uno32.D12, MTRX4.MISO
  N11: ChipKit_Uno32.A4, ZS-042_RTC.SDA, R1.Pin_0
  N12: ChipKit_Uno32.A5, ZS-042_RTC.SCL, R2.Pin_0
  3V3: ChipKit_Uno32.3V3, ESP-01.VCC

notes:
  UART
  I2C
  SPI

custom parts:
  chipKIT Uno32: Arduino-compatible prototyping platform
  ESP8266 ESP01: Generic WiFi Module based on the ESP8266 with onboard PCB antenna and UART communications
